# Fritzing sketch sketch (saved by Fritzing 0.7.12b)
breadboards: 1

parts:
  RaspberryPi1 = Raspberry Pi Model B
  Pi1 = Adafruit Pi Cobbler
  Continuos_Rotation_Servo = Basic Servo [part_number="Futaba S148"]
  BATT1 = 4xAA Switchable Battery Pack w/Bare Wire

nets:
  3V3: RaspberryPi1.3V3, Pi1.3V3
  5V: RaspberryPi1.5V, Pi1.5V0, Continuos_Rotation_Servo.vcc, BATT1.POS
  N1: RaspberryPi1.SDA, Pi1.SDA0
  N2: RaspberryPi1.SCL, Pi1.SCL0
  GND: RaspberryPi1.GND, Pi1.GND, Continuos_Rotation_Servo.gnd, BATT1.NEG
  N3: RaspberryPi1.#4, Pi1.PIN9
  N4: RaspberryPi1.TXD, Pi1.TXD
  N5: RaspberryPi1.RXD, Pi1.RXD
  N6: RaspberryPi1.#17, Pi1.#17
  N7: RaspberryPi1.#18, Pi1.#18, Continuos_Rotation_Servo.pulse
  N8: RaspberryPi1.#21, Pi1.#21
  N9: RaspberryPi1.#22, Pi1.#22
  N10: RaspberryPi1.#23, Pi1.#23
  N11: RaspberryPi1.#24, Pi1.#24
  N12: RaspberryPi1.MOSI, Pi1.MOSI
  N13: RaspberryPi1.MISO, Pi1.MISO
  N14: RaspberryPi1.#25, Pi1.#25
  N15: RaspberryPi1.SCLK, Pi1.SCLK
  N16: RaspberryPi1.CS0, Pi1.CE0
  N17: RaspberryPi1.CS1, Pi1.CE1

custom parts:
  Raspberry Pi Model B: Raspberry Pi (Model B)
  Adafruit Pi Cobbler: Adafruit Pi Cobbler GPIO Breakout for Raspberry Pi
  4xAA Switchable Battery Pack w/Bare Wire: 4xAA Switchable Battery Pack with Bare Wire connection
